# Fritzing sketch bmp_280_oled (saved by Fritzing 0.9.6b)
breadboards: 2

parts:
  M1 = BME280
  OLED_I2C1 = OLED 128x64 I2C Monochrome Display
  esp1 = ESP32 DevKitc V4

nets:
  VIN: M1.VIN, OLED_I2C1.VDD, esp1.3V3
  GND: M1.GND, OLED_I2C1.GND, esp1.GND#18
  N1: M1.SCL, OLED_I2C1.SCK, esp1.IO22
  N2: M1.SDA, OLED_I2C1.SDA

custom parts:
  BME280: Temperature Humidity Barometric presure Sensor
  ESP32 DevKitc V4: ESP32-DevKitC board with ESP32-WROOM-32 module. ESP32-DevKitC V4 is a small-sized ESP32-based development board produced by Espressif. Most of the pins on the ESP module are broken out to the pin headers on the board. The pins D0, D1, D2, D3, CMD and CLK are used internally for communication between ESP32 and SPI flash memory. They are grouped on both sides near the USB connector. Avoid using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
